// Logisim project cpu.circ as structural Verilog: 6 circuits, main circuit main
module main (
);

  wire [31:0] Instr;

  Clock clock_1 ();  // open: out
  ControlUnit controlunit_1 (.Instr(Instr));
  RegFile regfile_1 ();
  ALU alu_1 ();
  PC pc_1 (.Bdst({24{1'b0}}), .Br(1'b0), .Instr(Instr));

  // Notes on the sheet:
  //   Stage 3: EX
  //   Stage 1: IF
  //   Stage 2: ID
endmodule

module PC (
  input  [23:0] Bdst,
  input  Br,
  output [31:0] Instr
);

  wire CLK;
  wire [23:0] adder_1_out, nextPC, PC;

  Clock clock_1 (.out(CLK));
  Register #(.width(24)) register_1 (.D(nextPC), .en(1'b1), .clk(CLK), .Q(PC));  // open: clr
  Adder #(.width(24)) adder_1 (.a(PC), .b(24'h1), .out(adder_1_out));  // open: cin, cout
  RAM #(.addrWidth(24), .dataWidth(32), .enables("line")) Instruction_Memory (
    .addr(PC), .clk(CLK), .dout(Instr));  // open: we, din
  Multiplexer #(.width(24)) multiplexer_1 (.in0(adder_1_out), .in1(Bdst), .out(nextPC), .sel(Br));
endmodule

module RegFile (
);

  Register #(.width(32)) R0 ();  // open: D, en, clk, Q, clr
  Register #(.width(32)) R1 ();  // open: D, en, clk, Q, clr
  Register #(.width(32)) R2 ();  // open: D, en, clk, Q, clr
  Register #(.width(32)) R3 ();  // open: D, en, clk, Q, clr
  Register #(.width(32)) R4 ();  // open: D, en, clk, Q, clr
  Register #(.width(32)) R5 ();  // open: D, en, clk, Q, clr
  Register #(.width(32)) R6 ();  // open: D, en, clk, Q, clr
  Register #(.width(32)) R7 ();  // open: D, en, clk, Q, clr
  Register #(.width(32)) R8 ();  // open: D, en, clk, Q, clr
  Register #(.width(32)) R9 ();  // open: D, en, clk, Q, clr
  Register #(.width(32)) R10 ();  // open: D, en, clk, Q, clr
  Register #(.width(32)) R11 ();  // open: D, en, clk, Q, clr
  Register #(.width(32)) R12 ();  // open: D, en, clk, Q, clr
  Register #(.width(32)) R13 ();  // open: D, en, clk, Q, clr
  Register #(.width(32)) R14 ();  // open: D, en, clk, Q, clr
  Register #(.width(32)) R15 ();  // open: D, en, clk, Q, clr
  Register #(.width(32)) R16 ();  // open: D, en, clk, Q, clr
  Register #(.width(32)) R17 ();  // open: D, en, clk, Q, clr
  Register #(.width(32)) R18 ();  // open: D, en, clk, Q, clr
  Register #(.width(32)) R19 ();  // open: D, en, clk, Q, clr
  Register #(.width(32)) R20 ();  // open: D, en, clk, Q, clr
  Register #(.width(32)) R24 ();  // open: D, en, clk, Q, clr
  Register #(.width(32)) R21 ();  // open: D, en, clk, Q, clr
  Register #(.width(32)) R25 ();  // open: D, en, clk, Q, clr
  Register #(.width(32)) R22 ();  // open: D, en, clk, Q, clr
  Register #(.width(32)) R26 ();  // open: D, en, clk, Q, clr
  Register #(.width(32)) R23 ();  // open: D, en, clk, Q, clr
  Register #(.width(32)) R27 ();  // open: D, en, clk, Q, clr
  Register #(.width(32)) R28 ();  // open: D, en, clk, Q, clr
  Register #(.width(32)) R29 ();  // open: D, en, clk, Q, clr
  Register #(.width(32)) R30_SP ();  // open: D, en, clk, Q, clr
  Register #(.width(32)) R31_CMP ();  // open: D, en, clk, Q, clr
endmodule

module ALU (
);

  Adder adder_1 ();  // open: a, b, out, cin, cout
  Subtractor subtractor_1 ();  // open: a, b, out, bin, bout
  Multiplier multiplier_1 ();  // open: a, b, out, cin, cout
  Divider divider_1 ();  // open: a, b, out, upper, rem
  Negator negator_1 ();  // open: in, out
  Shifter shifter_1 ();  // open: in, dist, out
  Shifter #(.shift("lr")) shifter_2 ();  // open: in, dist, out
  Shifter #(.shift("ar")) shifter_3 ();  // open: in, dist, out
endmodule

module ControlUnit (
  input  [31:0] Instr
);
endmodule

module MEM (
);

  RAM ram_1 ();  // open: addr, we, oe, clk, din, dout
endmodule
